// Digital circuit adc-readout-analog-waveform-sampled-to-digital-outputs.dig as structural Verilog
module adc_readout_analog_waveform_sampled_to_digital_outputs (
);

  // AcVoltageSource Vs: pin names not known; wires that end beside it: 1'b0
  // Resistor R1: pin names not known
  // ADC ADC1: pin names not known
endmodule
