// Digital circuit dac-rc-filter-digital-input-produces-filtered-analog-voltage.dig as structural Verilog
module dac_rc_filter_digital_input_produces_filtered_analog_voltage (
  input  D0,
  input  D1,
  input  D2,
  input  D3
);

  // DAC dac_1: pin names not known; wires that end beside it: D0, D1, D2, D3
endmodule
