// Digital circuit digital-controlled-analog-switch-in-toggles-analog-path.dig as structural Verilog
module digital_controlled_analog_switch_in_toggles_analog_path (
  input  CTRL
);

  // DcVoltageSource Vs: pin names not known; wires that end beside it: CTRL, 1'b0
endmodule
