// Digital circuit mixed-transistor-gate-bjt-level-shifts-into-digital-and.dig as structural Verilog
module mixed_transistor_gate_bjt_level_shifts_into_digital_and (
);

  // DcVoltageSource Vcc: pin names not known; wires that end beside it: 1'b0
endmodule
