// Digital circuit pwm-to-analog-voltage-counter-generated-pwm-filtered-to-dc.dig as structural Verilog
module pwm_to_analog_voltage_counter_generated_pwm_filtered_to_dc (
  input  CLK
);

  Counter #(.simulationModel("digital")) CNT ();  // open: en, C, clr, out, ovf
endmodule
