// Digital circuit t-flip-flop-4-bit-ripple-counter.dig as structural Verilog
module t_flip_flop_4_bit_ripple_counter (
  input  CLK,
  output Q0,
  output Q1,
  output Q2,
  output Q3
);

  T_FF T1 (.T(CLK), .C(CLK), .Q(Q0));  // open: nQ
  T_FF T2 (.T(CLK), .C(Q0), .Q(Q1));  // open: nQ
  T_FF T3 (.T(CLK), .C(Q1), .Q(Q2));  // open: nQ
  T_FF T4 (.T(CLK), .C(Q2), .Q(Q3));  // open: nQ
  // also tied to VCC on the sheet: CLK
endmodule
